# Fritzing sketch Baofeng_Step_UP_Circuit (saved by Fritzing 0.9.6b)
stripboards: 1

parts:
  J1 = male pin header, 1 pin [form="♂ (male)"]
  J2 = male pin header, 1 pin [form="♂ (male)"]
  J3 = male pin header, 1 pin [form="♂ (male)"]
  J4 = male pin header, 1 pin [form="♂ (male)"]
  USB_Plug = USB TTL Serial Cable
  C1 = Electrolytic Capacitor [capacitance=1mF voltage=16V package="100 mil [THT, electrolytic]"]

nets:
  N1: J1.pin1, USB_Plug.GND
  N2: J2.pin1, USB_Plug.5V
  N3: J3.pin1, C1.-
  N4: J4.pin1, C1.+
  N5: USB_Plug.RX, USB_Plug.TX

notes:
  DC-DC Step UP Converter, 1A
  U_out = 7.4V
